// Logisim project SPRIND.circ as structural Verilog: 11 circuits, main circuit main
module main (
);

  wire Clock_inst_clk, reset_out, step_out, toggle_stepping_out;
  wire [15:0] Alu_inst_result, Memory_inst_o_data, sprind_registerfile_1_src1_out,
       sprind_registerfile_1_src2_out;

  Button toggle_stepping (.out(toggle_stepping_out));
  Button step (.out(step_out));
  Button reset (.out(reset_out));
  SPRIND_Clock Clock_inst (
    .step(step_out), .toggle_stepping(toggle_stepping_out), .rst(reset_out), .clk(Clock_inst_clk));
  SPRIND_Counter Counter_inst (
    .rst(reset_out), .clk(Clock_inst_clk), .mode_inc(1'b1));  // open: out_en, displacement, replacement, mode_replace, mode_displace, address
  SPRIND_RegisterFile sprind_registerfile_1 (
    .data_in(Memory_inst_o_data), .clk(Clock_inst_clk), .rst(reset_out),
    .src2_out(sprind_registerfile_1_src2_out), .src1_out(sprind_registerfile_1_src1_out));  // open: src2_reg_sel, dst_reg_sel, wr_en, i_out_en, src1_reg_sel
  SPRIND_Alu Alu_inst (
    .input0(sprind_registerfile_1_src1_out), .input1(sprind_registerfile_1_src2_out), .result(Alu_inst_result));  // open: i_carry, func, flags_updated, o_carry, overflow
  SPRIND_Memory Memory_inst (
    .i_address(Memory_inst_o_data), .i_data(Memory_inst_o_data), .o_data(Memory_inst_o_data));  // open: wr_en, out_en, clk
  SPRIND_TestStack TestStack_inst ();  // open: bit_in, op_push, op_pop, op_and, op_or, op_not, op_overwrite, data_in, en, clk, rst, state, top_of_stack
endmodule

module SPRIND_RegisterFile (
  input  i_out_en,
  input  [2:0] src1_reg_sel,
  input  [2:0] src2_reg_sel,
  input  [2:0] dst_reg_sel,
  input  [15:0] data_in,
  input  wr_en,
  input  clk,
  input  rst,
  output [15:0] src1_out,
  output [15:0] src2_out
);

  wire decoder_1_out0, decoder_1_out1, decoder_1_out2, decoder_1_out3, decoder_1_out4, decoder_1_out5,
       decoder_1_out6, decoder_1_out7;
  wire [15:0] a_q, b_q, multiplexer_1_out, multiplexer_2_out, sp_q, v_q, w_q, x_q, y_q, z_q;

  Decoder #(.select(3)) decoder_1 (
    .out0(decoder_1_out0), .out1(decoder_1_out1), .out2(decoder_1_out2), .out3(decoder_1_out3),
    .out4(decoder_1_out4), .out5(decoder_1_out5), .out6(decoder_1_out6), .out7(decoder_1_out7),
    .sel(dst_reg_sel), .en(wr_en));
  Register #(.width(16)) sp (.D(data_in), .en(decoder_1_out0), .clk(clk), .Q(sp_q), .clr(rst));
  Register #(.width(16)) x (.D(data_in), .en(decoder_1_out1), .clk(clk), .Q(x_q), .clr(rst));
  Register #(.width(16)) y (.D(data_in), .en(decoder_1_out2), .clk(clk), .Q(y_q), .clr(rst));
  Register #(.width(16)) z (.D(data_in), .en(decoder_1_out3), .clk(clk), .Q(z_q), .clr(rst));
  Register #(.width(16)) w (.D(data_in), .en(decoder_1_out4), .clk(clk), .Q(w_q), .clr(rst));
  Register #(.width(16)) v (.D(data_in), .en(decoder_1_out5), .clk(clk), .Q(v_q), .clr(rst));
  Register #(.width(16)) a (.D(data_in), .en(decoder_1_out6), .clk(clk), .Q(a_q), .clr(rst));
  Register #(.width(16)) b (.D(data_in), .en(decoder_1_out7), .clk(clk), .Q(b_q), .clr(rst));
  Multiplexer #(.select(3), .width(16)) multiplexer_1 (
    .in0(sp_q), .in1(x_q), .in2(y_q), .in3(z_q), .in4(w_q), .in5(v_q), .in6(a_q), .in7(b_q),
    .out(multiplexer_1_out), .sel(src1_reg_sel));
  Multiplexer #(.select(3), .width(16)) multiplexer_2 (
    .in0(sp_q), .in1(x_q), .in2(y_q), .in3(z_q), .in4(w_q), .in5(v_q), .in6(a_q), .in7(b_q),
    .out(multiplexer_2_out), .sel(src2_reg_sel));
  assign src1_out = i_out_en ? multiplexer_1_out : 16'bz;  // Controlled_Buffer controlled_buffer_1
  assign src2_out = i_out_en ? multiplexer_2_out : 16'bz;  // Controlled_Buffer controlled_buffer_2
endmodule

module SPRIND_Clock (
  input  step,
  input  toggle_stepping,
  input  rst,
  output clk
);

  wire and_1_out, clock_1_out, d_ff_1_q, j_k_ff_1_q, not_1_out;

  Clock clock_1 (.out(clock_1_out));
  D_Flip_Flop d_ff_1 (.D(toggle_stepping), .clk(clock_1_out), .Q(d_ff_1_q), .reset(rst));  // open: Qn, preset
  and and_1 (and_1_out, toggle_stepping, not_1_out);
  not not_1 (not_1_out, d_ff_1_q);
  J_K_Flip_Flop j_k_ff_1 (
    .J(and_1_out), .K(and_1_out), .clk(clock_1_out), .Q(j_k_ff_1_q), .reset(rst));  // open: Qn, preset
  Multiplexer multiplexer_1 (.in0(clock_1_out), .in1(step), .out(clk), .sel(j_k_ff_1_q));
  LED stepping (.in(j_k_ff_1_q));
endmodule

module SPRIND_Alu (
  input  i_carry,
  input  [3:0] func,
  input  [15:0] input0,
  input  [15:0] input1,
  output [15:0] result,
  output flags_updated,
  output o_carry,
  output overflow
);

  wire subtractor_1_bout;
  wire [15:0] adder_1_out, subtractor_1_out;

  Subtractor #(.width(16)) subtractor_1 (
    .a(input0), .b(input1), .out(subtractor_1_out), .bin(i_carry), .bout(subtractor_1_bout));
  Adder #(.width(16)) adder_1 (.a(input0), .b(input1), .out(adder_1_out), .cin(i_carry), .cout(o_carry));
  Multiplexer #(.select(4), .width(16)) multiplexer_1 (
    .in4(subtractor_1_out), .in6(adder_1_out), .out(result), .sel(func));  // open: in0, in1, in2, in3, in5, in7, in8, in9, in10, in11, in12, in13, in14, in15
  CheckOverflow checkoverflow_1 (.input0(input0), .input1(input1), .sum(adder_1_out), .out_4(overflow));
endmodule

module CheckOverflow (
  input  [15:0] input0,
  input  [15:0] input1,
  input  [15:0] sum,
  output out_4
);

  wire xnor_1_out, xor_1_out;

  xor xor_1 (xor_1_out, input1[15], sum[15]);
  xnor xnor_1 (xnor_1_out, input0[15], input1[15]);
  and and_1 (out_4, xnor_1_out, xor_1_out);
endmodule

module SPRIND_Counter (
  input  out_en,
  input  rst,
  input  clk,
  input  [14:0] displacement,
  input  [14:0] replacement,
  input  mode_inc,
  input  mode_replace,
  input  mode_displace,
  output [15:0] address
);

  wire or_1_out, or_2_out;
  wire [14:0] adder_1_out, counter_1_q, multiplexer_1_out;
  wire [15:0] bit_extender_1_out;

  Adder #(.width(15)) adder_1 (.a(counter_1_q), .b(displacement), .out(adder_1_out));  // open: cin, cout
  Multiplexer #(.width(15)) multiplexer_1 (
    .in0(adder_1_out), .in1(replacement), .out(multiplexer_1_out), .sel(mode_replace));
  or or_1 (or_1_out, mode_inc, mode_replace, mode_displace);
  or or_2 (or_2_out, mode_replace, mode_displace);
  Counter #(.max('h7fff), .width(15)) counter_1 (
    .clr(rst), .load(or_2_out), .up(1'b1), .count(or_1_out), .clk(clk), .D(multiplexer_1_out), .Q(counter_1_q));  // open: carry
  assign bit_extender_1_out = {{1{1'b0}}, counter_1_q};  // Bit_Extender bit_extender_1
  assign address = out_en ? bit_extender_1_out : 16'bz;  // Controlled_Buffer controlled_buffer_1
endmodule

module SPRIND_TestStack (
  input  bit_in,
  input  op_push,
  input  op_pop,
  input  op_and,
  input  op_or,
  input  op_not,
  input  op_overwrite,
  input  [15:0] data_in,
  input  en,
  input  clk,
  input  rst,
  output [15:0] state,
  output top_of_stack
);

  wire [15:0] BitStack_for_TestStack_o_state;

  Register #(.width(16)) TS (.D(BitStack_for_TestStack_o_state), .en(en), .clk(clk), .Q(state), .clr(rst));
  SPRIND_BitStack BitStack_for_TestStack (
    .i_state(state), .bit_in(bit_in), .op_push(op_push), .op_pop(op_pop), .op_and(op_and), .op_or(op_or),
    .op_not(op_not), .op_overwrite(op_overwrite), .data_in(data_in), .o_state(BitStack_for_TestStack_o_state));

  assign top_of_stack = state[0];
endmodule

module SPRIND_BitStack (
  input  [15:0] i_state,
  input  bit_in,
  input  op_push,
  input  op_pop,
  input  op_and,
  input  op_or,
  input  op_not,
  input  op_overwrite,
  input  [15:0] data_in,
  output [15:0] o_state
);

  wire and_3_out, not_1_out, or_3_out;
  wire [15:0] and_1_out, and_2_out, bit_extender_1_out, bit_extender_2_out, bit_extender_3_out,
       bit_extender_4_out, multiplexer_1_out, multiplexer_2_out, multiplexer_3_out, multiplexer_4_out,
       multiplexer_5_out, multiplexer_6_out, or_1_out, or_2_out, or_4_out, or_5_out, shifter_1_out,
       shifter_2_out;

  assign bit_extender_1_out = {{15{1'b0}}, bit_in};  // Bit_Extender bit_extender_1
  Multiplexer #(.width(16)) multiplexer_1 (
    .in0({16{1'b0}}), .in1(data_in), .out(multiplexer_1_out), .sel(op_overwrite));
  Shifter #(.width(16)) shifter_1 (.in(i_state), .\dist (4'b0001), .out(shifter_1_out));
  Shifter #(.shift("lr"), .width(16)) shifter_2 (.in(i_state), .\dist (4'b0001), .out(shifter_2_out));
  not not_1 (not_1_out, i_state[0]);
  assign or_1_out = shifter_1_out | bit_extender_1_out;  // OR_Gate or_1, 16 bits wide
  Multiplexer #(.width(16)) multiplexer_2 (
    .in0({16{1'b0}}), .in1(shifter_2_out), .out(multiplexer_2_out), .sel(op_pop));
  assign and_1_out = 16'hfffe & multiplexer_2_out;  // AND_Gate and_1, 16 bits wide
  assign bit_extender_2_out = {{15{1'b0}}, not_1_out};  // Bit_Extender bit_extender_2
  assign and_2_out = i_state & 16'hfffe;  // AND_Gate and_2, 16 bits wide
  Multiplexer #(.width(16)) multiplexer_3 (.in0({16{1'b0}}), .in1(or_1_out), .out(multiplexer_3_out), .sel(op_push));
  Multiplexer #(.width(16)) multiplexer_4 (.in0({16{1'b0}}), .in1(or_2_out), .out(multiplexer_4_out), .sel(op_not));
  assign or_2_out = bit_extender_2_out | and_2_out;  // OR_Gate or_2, 16 bits wide
  and and_3 (and_3_out, i_state[0], i_state[1]);
  or or_3 (or_3_out, i_state[0], i_state[1]);
  assign bit_extender_3_out = {{15{1'b0}}, and_3_out};  // Bit_Extender bit_extender_3
  assign or_4_out = bit_extender_3_out | and_1_out;  // OR_Gate or_4, 16 bits wide
  assign bit_extender_4_out = {{15{1'b0}}, or_3_out};  // Bit_Extender bit_extender_4
  assign or_5_out = bit_extender_4_out | and_1_out;  // OR_Gate or_5, 16 bits wide
  Multiplexer #(.width(16)) multiplexer_5 (.in0({16{1'b0}}), .in1(or_4_out), .out(multiplexer_5_out), .sel(op_and));
  Multiplexer #(.width(16)) multiplexer_6 (.in0({16{1'b0}}), .in1(or_5_out), .out(multiplexer_6_out), .sel(op_or));
  assign o_state = multiplexer_3_out | multiplexer_2_out | multiplexer_5_out | multiplexer_6_out | multiplexer_4_out | multiplexer_1_out;  // OR_Gate or_6, 16 bits wide
endmodule

module SPRIND_InstrDecoder (
  input  [15:0] i_instr,
  output [5:0] o_opcode,
  output [12:0] o_subr_imm13,
  output [7:0] o_li_imm8,
  output o_fmt_o,
  output [9:0] o_b_imm10,
  output [5:0] o_ri_imm6,
  output o_fmt_r,
  output [2:0] o_reg_r,
  output [2:0] o_reg_s,
  output [2:0] o_reg_t,
  output o_fmt_rr,
  output o_fmt_rrr,
  output o_fmt_ext,
  output o_fmt_ri,
  output o_fmt_li,
  output o_fmt_b,
  output o_fmt_subr,
  output o_fmt_rri
);

  wire nor_2_out, nor_3_out, nor_4_out, nor_5_out, nor_6_out, nor_9_out, nor_10_out, not_1_out, not_2_out,
       not_3_out, not_4_out, not_5_out, not_6_out, not_7_out, not_8_out, not_9_out, not_10_out, not_11_out,
       not_12_out, not_13_out, not_14_out, not_15_out, not_16_out;
  wire [5:0] bit_extender_1_out, bit_extender_2_out, bit_extender_3_out, bit_extender_4_out,
       bit_extender_5_out, bit_extender_6_out, bit_extender_7_out, bit_extender_8_out, bit_extender_9_out,
       bit_extender_10_out, bit_extender_11_out;

  nor nor_1 (o_fmt_o, i_instr[6], i_instr[7], i_instr[8], i_instr[9], i_instr[10], i_instr[11], i_instr[12], i_instr[13], i_instr[14], i_instr[15]);
  assign bit_extender_1_out = {{3{1'b0}}, i_instr[5:3]};  // Bit_Extender bit_extender_1
  not not_1 (not_1_out, i_instr[6]);
  nor nor_2 (nor_2_out, not_1_out, i_instr[7], i_instr[8], i_instr[9], i_instr[10], i_instr[11], i_instr[12], i_instr[13], i_instr[14], i_instr[15]);
  not not_2 (not_2_out, i_instr[7]);
  nor nor_3 (nor_3_out, not_2_out, i_instr[8], i_instr[9], i_instr[10], i_instr[11], i_instr[12], i_instr[13], i_instr[14], i_instr[15]);
  not not_3 (not_3_out, i_instr[8]);
  nor nor_4 (nor_4_out, not_3_out, i_instr[9], i_instr[10], i_instr[11], i_instr[12], i_instr[13], i_instr[14], i_instr[15]);
  assign bit_extender_2_out = {{3{1'b0}}, i_instr[8:6]};  // Bit_Extender bit_extender_2
  not not_4 (not_4_out, i_instr[9]);
  nor nor_5 (nor_5_out, not_4_out, i_instr[10], i_instr[11], i_instr[12], i_instr[13], i_instr[14], i_instr[15]);
  assign bit_extender_3_out = {{2{1'b0}}, i_instr[9:6]};  // Bit_Extender bit_extender_3
  not not_5 (not_5_out, i_instr[10]);
  nor nor_6 (nor_6_out, not_5_out, i_instr[11], i_instr[12], i_instr[13], i_instr[14], i_instr[15]);
  not not_6 (not_6_out, i_instr[11]);
  nor nor_7 (o_fmt_rrr, not_6_out, i_instr[12], i_instr[13], i_instr[14], i_instr[15]);
  not not_7 (not_7_out, i_instr[12]);
  nor nor_8 (o_fmt_ext, not_7_out, i_instr[13], i_instr[14], i_instr[15]);
  not not_8 (not_8_out, i_instr[13]);
  nor nor_9 (nor_9_out, not_8_out, i_instr[14], i_instr[15]);
  assign bit_extender_4_out = {{1{1'b0}}, i_instr[13:9]};  // Bit_Extender bit_extender_4
  not not_9 (not_9_out, i_instr[14]);
  nor nor_10 (nor_10_out, not_9_out, i_instr[15]);
  assign bit_extender_5_out = {{5{1'b0}}, i_instr[11]};  // Bit_Extender bit_extender_5
  nor nor_11 (o_fmt_li, i_instr[12], i_instr[13], i_instr[14], not_10_out);
  not not_10 (not_10_out, i_instr[15]);
  not not_11 (not_11_out, i_instr[12]);
  nor nor_12 (o_fmt_b, not_11_out, i_instr[13], i_instr[14], not_12_out);
  not not_12 (not_12_out, i_instr[15]);
  not not_13 (not_13_out, i_instr[13]);
  nor nor_13 (o_fmt_subr, not_13_out, i_instr[14], not_14_out);
  not not_14 (not_14_out, i_instr[15]);
  not not_15 (not_15_out, i_instr[14]);
  nor nor_14 (o_fmt_rri, not_15_out, not_16_out);
  not not_16 (not_16_out, i_instr[15]);
  assign o_opcode = o_fmt_o ? i_instr[5:0] : 6'bz;  // Controlled_Buffer controlled_buffer_1
  assign o_opcode = nor_2_out ? bit_extender_1_out : 6'bz;  // Controlled_Buffer controlled_buffer_2
  or or_1 (o_fmt_r, nor_2_out, nor_3_out);
  assign bit_extender_6_out = {{2{1'b0}}, i_instr[6:3]};  // Bit_Extender bit_extender_6
  assign bit_extender_7_out = {{4{1'b0}}, i_instr[7:6]};  // Bit_Extender bit_extender_7
  assign o_opcode = nor_4_out ? bit_extender_7_out : 6'bz;  // Controlled_Buffer controlled_buffer_3
  assign o_opcode = nor_5_out ? bit_extender_2_out : 6'bz;  // Controlled_Buffer controlled_buffer_4
  or or_2 (o_fmt_rr, nor_4_out, nor_5_out, nor_6_out);
  assign o_opcode = nor_6_out ? bit_extender_3_out : 6'bz;  // Controlled_Buffer controlled_buffer_5
  assign bit_extender_8_out = {{4{1'b0}}, i_instr[10:9]};  // Bit_Extender bit_extender_8
  assign o_opcode = o_fmt_rrr ? bit_extender_8_out : 6'bz;  // Controlled_Buffer controlled_buffer_6
  assign o_opcode = o_fmt_ext ? {6{1'b1}} : 6'bz;  // Controlled_Buffer controlled_buffer_7
  assign bit_extender_9_out = {{2{1'b0}}, i_instr[12:9]};  // Bit_Extender bit_extender_9
  assign o_opcode = nor_9_out ? bit_extender_9_out : 6'bz;  // Controlled_Buffer controlled_buffer_8
  or or_3 (o_fmt_ri, nor_9_out, nor_10_out);
  assign o_opcode = nor_10_out ? bit_extender_4_out : 6'bz;  // Controlled_Buffer controlled_buffer_9
  assign o_opcode = o_fmt_li ? bit_extender_5_out : 6'bz;  // Controlled_Buffer controlled_buffer_10
  assign bit_extender_10_out = {{4{1'b0}}, i_instr[11:10]};  // Bit_Extender bit_extender_10
  assign o_opcode = o_fmt_b ? bit_extender_10_out : 6'bz;  // Controlled_Buffer controlled_buffer_11
  assign o_opcode = o_fmt_subr ? {6{1'b0}} : 6'bz;  // Controlled_Buffer controlled_buffer_12
  assign bit_extender_11_out = {{4{1'b0}}, i_instr[13:12]};  // Bit_Extender bit_extender_11
  assign o_opcode = o_fmt_rri ? bit_extender_11_out : 6'bz;  // Controlled_Buffer controlled_buffer_13
  assign o_opcode = nor_3_out ? bit_extender_6_out : 6'bz;  // Controlled_Buffer controlled_buffer_14

  assign o_b_imm10 = i_instr[9:0];
  assign o_li_imm8 = i_instr[10:3];
  assign o_reg_r = i_instr[2:0];
  assign o_reg_s = i_instr[5:3];
  assign o_reg_t = i_instr[8:6];
  assign o_ri_imm6 = i_instr[8:3];
  assign o_subr_imm13 = i_instr[12:0];
endmodule

module SPRIND_ControlUnit (
  input  [15:0] i_instr
);

  SPRIND_InstrDecoder sprind_instrdecoder_1 (.i_instr(i_instr));  // open: o_subr_imm13, o_li_imm8, o_b_imm10, o_reg_r, o_reg_s, o_reg_t, o_ri_imm6, o_fmt_o, o_fmt_r, o_fmt_rr, o_fmt_rrr, o_fmt_ext, o_fmt_ri, o_fmt_li, o_fmt_b, o_fmt_subr, o_fmt_rri, o_opcode
endmodule

module SPRIND_Memory (
  input  [15:0] i_address,
  input  wr_en,
  input  out_en,
  input  clk,
  input  [15:0] i_data,
  output [15:0] o_data
);

  RAM #(.addrWidth(16), .dataWidth(16)) ram1 (
    .addr(i_address), .we(wr_en), .oe(out_en), .clk(clk), .din(i_data), .dout(o_data));
endmodule
